# Fritzing sketch piSchoolBell (saved by Fritzing 0.9.2b)
breadboards: 1

parts:
  Raspberry_Pi_1 = Raspberry Pi 3 [part_number=RPI-3-V1.2]
  U1 = LCD-16X2 [package=lcd-16x2_nosilk]
  R1 = Trimmer Potentiometer [maximum_resistance=10kΩ package=THT]
  S1 = Pushbutton [package="[THT]"]
  S2 = Pushbutton [package="[THT]"]
  Part1 = KY-019 5V Relay Module [package="Breakout board"]
  S3 = Toggle Switch [package=THT]
  R2 = Resistor [tolerance=±5% resistance=10k package=THT]
  R3 = Resistor [tolerance=±5% resistance=10k package=THT]
  R4 = Resistor [tolerance=±5% resistance=1k package=THT]
  R5 = Resistor [tolerance=±5% resistance=1k package=THT]
  U2 = Transformer [package=transformer_smd]

nets:
  N1: Raspberry_Pi_1.3V3, U1.A
  GND: Raspberry_Pi_1.GND, U1.VSS, U1.R_W, U1.K, S1.Pin_3, S1.Pin_4, S2.Pin_3, S2.Pin_4, Part1.-, R2.Pin_1, R3.Pin_1, R4.Pin_0, R5.Pin_0
  N2: Raspberry_Pi_1.GIPO6, U1.DB4
  N3: Raspberry_Pi_1.GIPO13, U1.DB5
  N4: Raspberry_Pi_1.GIPO19, U1.DB6
  N5: Raspberry_Pi_1.GIPO26, U1.DB7
  N6: Raspberry_Pi_1.GIPO21, U1.E
  N7: Raspberry_Pi_1.GIPO20, U1.RS
  N8: Raspberry_Pi_1.GIPO7, R4.Pin_1
  N9: Raspberry_Pi_1.GIPO8, R5.Pin_1
  N10: Raspberry_Pi_1.GIPO15, Part1.S
  5V: Raspberry_Pi_1.5V, U1.VDD, Part1.+, R2.Pin_0, R3.Pin_0
  N11: U1.VO, R1.wiper
  N12: S1.Pin_1, S1.Pin_2
  N13: S2.Pin_1, S2.Pin_2
  N14: Part1.Common, U2.4
  N15: Part1.NO, S3.COM

notes:
  School bell

custom parts:
  KY-019 5V Relay Module: KY-019 5V Relay module, used to control AC circuits.
